# Fritzing sketch schema-de-montaj (saved by Fritzing 1.0.1rc)
breadboards: 1

parts:
  YwRobot_Power_Supply1 = YwRobot Breadboard Power Supply [part_number=545043]
  JACK1 = 2.1mm Barrel Jack with Terminal Block
  LED2 = LED - 5mm [color="Green (555nm)" current=0.030A package="5 mm [THT]"]
  LED3 = LED - 5mm [color="Yellow (585nm)" current=0.030A package="5 mm [THT]"]
  LED4 = LED - 5mm [color="Red (633nm)" current=0.030A package="5 mm [THT]"]
  M1 = DOIT Esp32 DevKit v1 (30 pins long, 11 pins width) [part_number=ESP32S-PIN30]
  Parte1 = RFID-RC522-v2
  Parte2 = LCD1602-I2C
  J1 = Basic Servo
  VCC1 = 4 x AAA Battery Mount

nets:
  VCC: YwRobot_Power_Supply1.VCC#5, Parte2.VCC, J1.vcc
  GND: YwRobot_Power_Supply1.GND#11, LED2.cathode, LED3.cathode, LED4.cathode, Parte2.GND, J1.gnd
  N1: JACK1.POS, VCC1.+
  N2: JACK1.NEG, VCC1.-
  N3: LED2.anode, M1.D25
  N4: LED3.anode, M1.D33
  N5: LED4.anode, M1.D32
  3V3: M1.3V3, Parte1.3.3V
  GND_2: M1.GND, Parte1.GND
  N6: M1.D4, Parte1.RST
  N7: M1.D5, Parte1.SDA
  N8: M1.D18, Parte1.SCK
  N9: M1.D19, Parte1.MISO
  N10: M1.D21, Parte2.SCL
  N11: M1.D22, Parte2.SDA
  N12: M1.D23, Parte1.MOSI
  N13: M1.D26, J1.pulse

custom parts:
  YwRobot Breadboard Power Supply: The YwRobot Breadboard Power Supply (MB-V2) has two power rails; they can be 5V or 3V3. Power to the module can be provided through the female USB socket or through the A10 (female) 2.1mm power jack.
  DOIT Esp32 DevKit v1 (30 pins long, 11 pins width): The DOIT Esp32 DevKit v1 is one of the development board created by DOIT to evaluate the ESP-WROOM-32 module. It is based on the ESP32 microcontroller that boasts Wifi, Bluetooth, Ethernet and Low Power support all in a single chip. (vanepp) made breadboard work, adjusted pin numbering and labels and reduced size of schematic and cleaned up pcb. This chip is 30pins long (2 x15) and 11 pins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
  RFID-RC522-v2: A simple China made RFID-RC522 Reader; do check the pin labels, as this is a MFRC522 based clone.
  LCD1602-I2C: A standard character display, usually with 2x16 characters. Comes in many colors with LCM1602 IIC attached.
